// Logisim project P6.circ as structural Verilog: 1 circuit, main circuit main
module main (
  input  A,
  input  B,
  input  C,
  output X
);

  wire AND_2_out, AND_3_out, AND_out;

  and AND (AND_out, A, B);
  and AND_2 (AND_2_out, A, C);
  and AND_3 (AND_3_out, A, B, C);
  or or_1 (X, AND_out, AND_2_out, AND_3_out);

  // Notes on the sheet:
  //   D=A.B
  //   E=A.C
  //   F=A.B.C
  //   G=D+E+F
endmodule
