// Logisim project booleanexp1.circ as structural Verilog: 1 circuit, main circuit main
module main (
  input  B,
  input  A,
  output F1
);

  wire AND_2_out, AND_out, NOT_out;

  not NOT (NOT_out, B);
  and AND (AND_out, NOT_out, A);
  and AND_2 (AND_2_out, B, A);
  or OR (F1, AND_out, AND_2_out);

  // Notes on the sheet:
  //   1
  //   2
  //   1
  //   2
  //   4
  //   5
  //   3
  //   6
  //   1
  //   2
  //   3
endmodule
