// Logisim project comparter1.circ as structural Verilog: 1 circuit, main circuit main
module main (
  input  [7:0] in_1,
  input  [7:0] in_2
);

  wire comparator_1_eq, comparator_1_gt, comparator_1_lt;

  LED led_1 (.in(comparator_1_gt));
  Comparator comparator_1 (.a(in_1), .b(in_2), .gt(comparator_1_gt), .eq(comparator_1_eq), .lt(comparator_1_lt));
  LED led_2 (.in(comparator_1_eq));
  LED led_3 (.in(comparator_1_lt));

  // Notes on the sheet:
  //   A
  //   B
endmodule
