// Logisim project decoder1.circ as structural Verilog: 1 circuit, main circuit main
module main (
  input  in_1,
  input  [1:0] in_2,
  output out_3,
  output out_4,
  output out_5,
  output out_6
);

  Decoder #(.select(2)) decoder_1 (.out0(out_3), .out1(out_4), .out2(out_5), .out3(out_6), .sel(in_2), .en(in_1));
endmodule
