// Logisim project demux1.circ as structural Verilog: 1 circuit, main circuit main
module main (
  input  in_1,
  input  S
);

  wire demultiplexer_1_out0, demultiplexer_1_out1;

  Demultiplexer demultiplexer_1 (
    .out0(demultiplexer_1_out0), .out1(demultiplexer_1_out1), .in(in_1), .sel(S));  // open: en
  LED led_1 (.in(demultiplexer_1_out0));
  LED led_2 (.in(demultiplexer_1_out1));
endmodule
