// Logisim project encoder1.circ as structural Verilog: 1 circuit, main circuit main
module main (
  input  in_1,
  input  ENABLE,
  output _0,
  output _1
);

  Priority_Encoder #(.select(1)) priority_encoder_1 (
    .in0(in_1), .out(_0), .gs(_1), .en_in(ENABLE));  // open: in1, en_out
endmodule
