// Logisim project encoder2.circ as structural Verilog: 1 circuit, main circuit main
module main (
  input  in_1,
  input  in_2,
  input  in_3,
  input  in_4,
  input  in_5,
  output [1:0] out_6,
  output out_7
);

  Priority_Encoder #(.select(2)) priority_encoder_1 (
    .in0(in_1), .in1(in_2), .in2(in_3), .in3(in_5), .out(out_6), .gs(out_7), .en_in(in_4));  // open: en_out
endmodule
