// Logisim project fourby1.circ as structural Verilog: 1 circuit, main circuit main
module main (
  input  i0,
  input  i1,
  input  i2,
  input  i4,
  input  [1:0] SOS1
);

  wire multiplexer_1_out;

  Multiplexer #(.select(2)) multiplexer_1 (
    .in0(i0), .in1(i1), .in2(i2), .in3(i4), .out(multiplexer_1_out), .sel(SOS1));  // open: en
  LED Y (.in(multiplexer_1_out));
endmodule
