// Logisim project gate1.circ as structural Verilog: 1 circuit, main circuit main
module main (
  input  NOT,
  input  in_2,
  output out_3
);

  wire AND_out, not_1_out, or_1_out;

  not not_1 (not_1_out, NOT);
  or or_1 (or_1_out, NOT, in_2);
  and AND (AND_out, not_1_out, or_1_out);
  or or_2 (out_3, AND_out, or_1_out);
endmodule
