// Logisim project gate3.circ as structural Verilog: 1 circuit, main circuit main
module main (
  input  A,
  input  B,
  input  C,
  output Y
);

  wire AND_out, not_1_out;

  and AND (AND_out, A, B);
  not not_1 (not_1_out, C);
  and AND_2 (Y, AND_out, B, not_1_out);

  // Notes on the sheet:
  //   NOT
endmodule
