// Logisim project gate4.circ as structural Verilog: 1 circuit, main circuit main
module main (
  input  A,
  input  B,
  input  C,
  output Y
);

  wire AND_2_out, AND_out, not_1_out, not_2_out, OR_out;

  not not_1 (not_1_out, B);
  not not_2 (not_2_out, C);
  and AND (AND_out, A, B, C);
  or OR (OR_out, not_1_out, not_2_out);
  and AND_2 (AND_2_out, A, OR_out);
  or OR_2 (Y, AND_out, AND_2_out);

  // Notes on the sheet:
  //   NOT
  //   NOT
endmodule
