// Logisim project gate5.circ as structural Verilog: 1 circuit, main circuit main
module main (
  input  in_1,
  input  in_2,
  input  in_3,
  input  in_4,
  output out_5
);

  wire and_1_out, not_1_out, not_2_out, or_1_out, or_2_out, or_3_out;

  not not_1 (not_1_out, in_4);
  and and_1 (and_1_out, in_1, not_1_out);
  or or_1 (or_1_out, in_1, in_4);
  or or_2 (or_2_out, in_3, or_1_out);
  or or_3 (or_3_out, and_1_out, in_2);
  not not_2 (not_2_out, or_2_out);
  or or_4 (out_5, or_3_out, not_2_out);
endmodule
