// Logisim project gate8.circ as structural Verilog: 1 circuit, main circuit main
module main (
  input  A,
  input  B,
  input  C,
  output X,
  output Y
);

  wire AND_2_out, AND_3_out, AND_out;

  or OR (X, A, B, C);
  and AND (AND_out, C, C);
  and AND_2 (AND_2_out, C, C);
  and AND_3 (AND_3_out, C, C);
  or OR_2 (Y, AND_out, AND_2_out, AND_3_out);
endmodule
